// Logisim project Double-Traffic-Control.circ as structural Verilog: 4 circuits, main circuit Traffic UI
module main (
  input  Clock,
  input  [2:0] Traffic_Type,
  output R1,
  output Y1,
  output G1,
  output R2,
  output Y2,
  output G2
);

  wire [2:0] rom_1_data, rom_2_data, rom_3_data, rom_4_data, rom_5_data, rom_6_data, rom_7_data, rom_8_data,
       rom_9_data, rom_10_data;
  wire [5:0] counter_1_q;

  Counter #(.width(6), .max('h3f)) counter_1 (
    .count(Clock), .Q(counter_1_q), .clk(Clock));  // open: load, D, carry, clr
  ROM #(.addrWidth(6), .dataWidth(3)) rom_1 (.addr(counter_1_q), .data(rom_1_data));  // open: sel
  ROM #(.addrWidth(6), .dataWidth(3)) rom_2 (.addr(counter_1_q), .data(rom_2_data));  // open: sel
  ROM #(.addrWidth(6), .dataWidth(3)) rom_3 (.addr(counter_1_q), .data(rom_3_data));  // open: sel
  ROM #(.addrWidth(6), .dataWidth(3)) rom_4 (.addr(counter_1_q), .data(rom_4_data));  // open: sel
  ROM #(.addrWidth(6), .dataWidth(3)) rom_5 (.addr(counter_1_q), .data(rom_5_data));  // open: sel
  ROM #(.addrWidth(6), .dataWidth(3)) rom_6 (.addr(counter_1_q), .data(rom_6_data));  // open: sel
  ROM #(.addrWidth(6), .dataWidth(3)) rom_7 (.addr(counter_1_q), .data(rom_7_data));  // open: sel
  ROM #(.addrWidth(6), .dataWidth(3)) rom_8 (.addr(counter_1_q), .data(rom_8_data));  // open: sel
  ROM #(.addrWidth(6), .dataWidth(3)) rom_9 (.addr(counter_1_q), .data(rom_9_data));  // open: sel
  ROM #(.addrWidth(6), .dataWidth(3)) rom_10 (.addr(counter_1_q), .data(rom_10_data));  // open: sel
  Multiplexer #(.select(3), .width(6)) multiplexer_1 (
    .in0({rom_2_data, rom_1_data}), .in1({rom_4_data, rom_3_data}), .in2({rom_6_data, rom_5_data}),
    .in3({rom_8_data, rom_7_data}), .in4({rom_10_data, rom_9_data}), .out({G2, Y2, R2, G1, Y1, R1}),
    .sel(Traffic_Type));  // open: in5, in6, in7, en

  // Notes on the sheet:
  //   contents of rom_1 (hex, n*v repeats v):
  //   28*1 4*3 28*4 4*6
  //   contents of rom_2 (hex, n*v repeats v):
  //   28*4 4*6 28*1 4*3
  //   contents of rom_3 (hex, n*v repeats v):
  //   44*1 4*3 12*4 4*6
  //   contents of rom_4 (hex, n*v repeats v):
  //   44*4 4*6 12*1 4*3
  //   contents of rom_5 (hex, n*v repeats v):
  //   12*1 4*3 44*4 4*6
  //   contents of rom_6 (hex, n*v repeats v):
  //   12*4 4*6 44*1 4*3
  //   contents of rom_7 (hex, n*v repeats v):
  //   2 0 2 0 2 0 2 0 2 0 2 0 2 0 2 0 2 0 2 0 2 0 2 0 2 0 2 0 2 0 2 0 2 0 2 0 2 0 2 0 2 0 2 0 2 0 2 0 2 0
  //   2 0 2 0 2 0 2 0 2 0 2 0 2
  //   contents of rom_8 (hex, n*v repeats v):
  //   2 0 2 0 2 0 2 0 2 0 2 0 2 0 2 0 2 0 2 0 2 0 2 0 2 0 2 0 2 0 2 0 2 0 2 0 2 0 2 0 2 0 2 0 2 0 2 0 2 0
  //   2 0 2 0 2 0 2 0 2 0 2 0 2
  //   contents of rom_9 (hex, n*v repeats v):
  //   64*1
  //   contents of rom_10 (hex, n*v repeats v):
  //   64*1
endmodule

module Traffic_UI (
  input  [2:0] Mode_Selection_Pin
);

  wire clock_1_out, clock_2_out, G1, G2, GC, GC2, GP, GP2, Pedestrian_Switch_2_out, Pedestrian_Switch_out,
       R1, R2, RC, RC2, RP, RP2, Y1, Y2;
  wire [2:0] multiplexer_1_out;
  wire [3:0] hex_to_decimal_1_output_1, hex_to_decimal_1_output_2, hex_to_decimal_2_output_1,
       hex_to_decimal_2_output_2, hex_to_decimal_3_output_1, hex_to_decimal_3_output_2;
  wire [5:0] counter_1_q, counter_2_q, counter_3_q;
  wire [7:0] adder_1_out, bit_extender_1_out, bit_extender_2_out, bit_extender_3_out;

  Clock clock_1 (.out(clock_1_out));
  Button Pedestrian_Switch (.out(Pedestrian_Switch_out));
  Counter #(.width(6), .max('h3f)) counter_1 (
    .count(clock_1_out), .Q(counter_1_q), .clk(clock_1_out));  // open: load, D, carry, clr
  main main_1 (
    .R1(R1), .Y1(Y1), .G1(G1), .R2(R2), .Y2(Y2), .G2(G2), .Traffic_Type(multiplexer_1_out),
    .Clock(clock_1_out));
  Pedestrian_Lights pedestrian_lights_1 (
    .Clock(clock_1_out), .Pedestrian_Switch(Pedestrian_Switch_out), .RC(RC), .GC(GC), .RP(RP), .GP(GP));
  Adder adder_1 (.a(8'h1), .b(bit_extender_1_out), .out(adder_1_out));  // open: cin, cout
  assign bit_extender_1_out = {{2{1'b0}}, counter_1_q};  // Bit_Extender bit_extender_1
  Counter #(.width(6), .max('h1f)) counter_2 (
    .load(clock_1_out), .Q(counter_2_q), .clk(clock_1_out), .clr(GC));  // open: D, count, carry
  Hex_Digit_Display hex_digit_display_1 (.value(hex_to_decimal_1_output_1));  // open: dp
  Hex_to_Decimal hex_to_decimal_1 (
    .Input(adder_1_out), .Output_1(hex_to_decimal_1_output_1), .Output_2(hex_to_decimal_1_output_2));
  Multiplexer #(.select(3), .width(3)) multiplexer_1 (
    .in0(3'b000), .in1(3'b001), .in2(3'b010), .in3(3'b011), .in4(3'b100), .out(multiplexer_1_out),
    .sel(Mode_Selection_Pin));  // open: in5, in6, in7, en
  assign bit_extender_2_out = {{2{1'b0}}, counter_2_q};  // Bit_Extender bit_extender_2
  LED led_1 (.in(GC));
  LED led_2 (.in(RP));
  LED led_3 (.in(GP));
  LED led_4 (.in(RC));
  LED led_5 (.in(RC));
  LED led_6 (.in(RP));
  LED led_7 (.in(GP));
  LED led_8 (.in(GC));
  // Probe on Mode_Selection_Pin
  Hex_Digit_Display hex_digit_display_2 (.value(hex_to_decimal_1_output_2));  // open: dp
  Hex_to_Decimal hex_to_decimal_2 (
    .Input(bit_extender_2_out), .Output_1(hex_to_decimal_2_output_1), .Output_2(hex_to_decimal_2_output_2));
  Hex_Digit_Display hex_digit_display_3 (.value(hex_to_decimal_2_output_2));  // open: dp
  Hex_Digit_Display hex_digit_display_4 (.value(hex_to_decimal_2_output_1));  // open: dp
  Clock clock_2 (.out(clock_2_out));
  LED led_9 (.in(RP2));
  LED led_10 (.in(GP2));
  LED led_11 (.in(GC2));
  LED led_12 (.in(R1));
  LED led_13 (.in(Y1));
  LED led_14 (.in(R2));
  LED led_15 (.in(Y2));
  LED led_16 (.in(G2));
  Button Pedestrian_Switch_2 (.out(Pedestrian_Switch_2_out));
  LED led_17 (.in(RC2));
  LED led_18 (.in(G1));
  Pedestrian_Lights pedestrian_lights_2 (
    .Clock(clock_2_out), .Pedestrian_Switch(Pedestrian_Switch_2_out), .RC(RC2), .GC(GC2), .RP(RP2), .GP(GP2));
  Counter #(.width(6), .max('h1f)) counter_3 (
    .load(clock_2_out), .Q(counter_3_q), .clk(clock_2_out), .clr(RP2));  // open: D, count, carry
  LED led_19 (.in(RC2));
  LED led_20 (.in(GC2));
  LED led_21 (.in(RP2));
  LED led_22 (.in(GP2));
  LED led_23 (.in(R2));
  LED led_24 (.in(Y2));
  LED led_25 (.in(G2));
  LED led_26 (.in(Y1));
  LED led_27 (.in(G1));
  LED led_28 (.in(R1));
  assign bit_extender_3_out = {{2{1'b0}}, counter_3_q};  // Bit_Extender bit_extender_3
  Hex_Digit_Display hex_digit_display_5 (.value(hex_to_decimal_3_output_1));  // open: dp
  Hex_Digit_Display hex_digit_display_6 (.value(hex_to_decimal_3_output_2));  // open: dp
  Hex_to_Decimal hex_to_decimal_3 (
    .Input(bit_extender_3_out), .Output_1(hex_to_decimal_3_output_1), .Output_2(hex_to_decimal_3_output_2));

  // Notes on the sheet:
  //   Pedestrian Crosswalk System
  //   Intersection Traffic System
  //   0 - Normal traffic
  //   1 - Heavy traffic on system 2
  //   2- Heavy traffic on system 1
  //   3 - Blinking yellow (not functional lights)
  //   4 - All red (intersection blocked)
  //   Pedestrian Crosswalk System 2
endmodule

module Pedestrian_Lights (
  input  Clock,
  input  Pedestrian_Switch,
  output RC,
  output GC,
  output RP,
  output GP
);

  wire and_1_out, comparator_1_eq, comparator_2_eq, or_1_out, or_2_out, or_3_out, t_ff_1_q, t_ff_2_q;
  wire [1:0] rom_1_data, rom_2_data, rom_3_data, rom_4_data;
  wire [5:0] counter_1_q;

  Counter #(.width(6), .max('h3f)) counter_1 (
    .count(Clock), .Q(counter_1_q), .clk(Clock));  // open: load, D, carry, clr
  Comparator #(.width(6)) comparator_1 (.a(counter_1_q), .b({6{1'b0}}), .eq(comparator_1_eq));  // open: gt, lt
  Comparator #(.width(6)) comparator_2 (.a(counter_1_q), .b(6'b100000), .eq(comparator_2_eq));  // open: gt, lt
  or or_1 (or_1_out, Pedestrian_Switch, t_ff_2_q);
  T_Flip_Flop t_ff_1 (.clk(or_1_out), .T(or_1_out), .Q(t_ff_1_q));  // open: Qn, preset, reset, en
  ROM #(.addrWidth(6), .dataWidth(2)) rom_1 (.addr(counter_1_q), .data(rom_1_data));  // open: sel
  ROM #(.addrWidth(6), .dataWidth(2)) rom_2 (.addr(counter_1_q), .data(rom_2_data));  // open: sel
  ROM #(.addrWidth(6), .dataWidth(2)) rom_3 (.addr(counter_1_q), .data(rom_3_data));  // open: sel
  ROM #(.addrWidth(6), .dataWidth(2)) rom_4 (.addr(counter_1_q), .data(rom_4_data));  // open: sel
  or or_2 (or_2_out, comparator_1_eq, comparator_2_eq);
  or or_3 (or_3_out, t_ff_1_q, t_ff_2_q);
  T_Flip_Flop t_ff_2 (.clk(and_1_out), .T(and_1_out), .Q(t_ff_2_q));  // open: Qn, preset, reset, en
  and and_1 (and_1_out, or_2_out, or_3_out);
  Multiplexer #(.width(4)) multiplexer_1 (
    .in0({rom_2_data, rom_1_data}), .in1({rom_4_data, rom_3_data}), .out({GP, RP, GC, RC}), .sel(t_ff_2_q));  // open: en

  // Notes on the sheet:
  //   contents of rom_1 (hex, n*v repeats v):
  //   64*2
  //   contents of rom_2 (hex, n*v repeats v):
  //   64*1
  //   contents of rom_3 (hex, n*v repeats v):
  //   64*1
  //   contents of rom_4 (hex, n*v repeats v):
  //   64*2
endmodule

module Hex_to_Decimal (
  input  [7:0] Input,
  output [3:0] Output_1,
  output [3:0] Output_2
);

  wire [7:4] divider_1_out, divider_1_rem;

  Divider divider_1 (
    .a(Input), .b(8'ha), .out({divider_1_out, Output_1}), .rem({divider_1_rem, Output_2}));  // open: upper
endmodule
